# Fritzing sketch door_lock (saved by Fritzing 0.9.3b)

parts:
  Part1 = Bluetooth HC-05 Macho
  Part2 = Arduino Uno (Rev3) - ICSP
  VCC1 = 4 x AAA Battery Mount
  L2 = Solenoid
  KY-1 = Keyes Relay [package=THT]

nets:
  N1: Part1.TXD, Part2.D0/RX
  N2: Part1.RXD, Part2.D1/TX
  VCC: Part1.VCC, Part2.5V
  GND: Part1.GND, Part2.GND, KY-1.ground
  N3: Part2.D13/SCK, KY-1.signal
  N4: Part2.IOREF, KY-1.power
  N5: VCC1.+, KY-1.NC
  N6: L2.pin2, KY-1.C

custom parts:
  Keyes Relay: The Keyes 5V relay module is suitable for SCM development, home appliance control. It uses a 5V~12V TIL control signal which can control DC / AC signal.
