# Fritzing sketch NEO_6M_GPS (saved by Fritzing 0.9.3b)

parts:
  Bauteil1 = Arduino Uno (Rev3)
  GY-NEO6MV2 = SUP500F [package=sup500f]

nets:
  N1: Bauteil1.D0/RX, GY-NEO6MV2.VCC
  N2: Bauteil1.D1/TX, GY-NEO6MV2.GND
  N3: Bauteil1.3V3, GY-NEO6MV2.TX-O
  N4: Bauteil1.GND, GY-NEO6MV2.RX-I

notes:
  GND:Black
  VCC: Red
  RX: Brown
  TX: Green
