# Fritzing sketch RGB_Led_Controlled_By_Voice (saved by Fritzing 0.9.3b)
breadboards: 1

parts:
  LED1 = RGB LED (com. cathode, rgb) [package="5 mm [THT]"]
  Part2 = Bluetooth HC-05 Macho
  R1 = Resistor [tolerance=±5% resistance=220 package="0805 [SMD]"]
  R2 = Resistor [tolerance=±5% resistance=220 package="0805 [SMD]"]
  R3 = Resistor [tolerance=±5% resistance=220 package="0805 [SMD]"]
  Part1 = Arduino Uno (Rev3) - ICSP

nets:
  N1: LED1.red_anode, R3.Pin_0
  GND: LED1.common_cathode, Part2.GND, Part1.GND
  N2: LED1.green_anode, R1.Pin_0
  N3: LED1.blue_anode, R2.Pin_0
  N4: Part2.TXD, Part1.D0/RX
  N5: Part2.RXD, Part1.D1/TX
  VCC: Part2.VCC, Part1.5V
  N6: R1.Pin_1, Part1.D12/MISO
  N7: R2.Pin_1, Part1.D13/SCK
  N8: R3.Pin_1, Part1.D11_PWM/MOSI
