# Fritzing sketch Wifi_Control_Car (saved by Fritzing 0.9.3b)

parts:
  VCC1 = Battery
  M6 = DC Motor
  M7 = DC Motor
  M8 = DC Motor
  M9 = DC Motor
  M10 = DOIT Esp32 DevKit v1 (30 pins long, 11 pins width) [part_number=ESP32S-PIN30]
  S2 = H-Bridge with L298N

nets:
  GND: VCC1.-, M10.GND, S2.GND
  N1: VCC1.+, S2.12V
  N2: M6.pin_1, M9.pin_1, S2.OUT3-Motor2
  N3: M6.pin_2, M9.pin_2, S2.OUT4-Motor2
  N4: M7.pin_2, M8.pin_2, S2.OUT2-Motor1
  N5: M8.pin_1, S2.OUT1-Motor1
  N6: M10.D2, S2.IN1
  N7: M10.D4, S2.IN2
  N8: M10.D18, S2.IN3
  N9: M10.D19, S2.IN4
  VIN: M10.VIN, S2.5V

custom parts:
  DOIT Esp32 DevKit v1 (30 pins long, 11 pins width): The DOIT Esp32 DevKit v1 is one of the development board created by DOIT to evaluate the ESP-WROOM-32 module. It is based on the ESP32 microcontroller that boasts Wifi, Bluetooth, Ethernet and Low Power support all in a single chip. (vanepp) made breadboard work, adjusted pin numbering and labels and reduced size of schematic and cleaned up pcb. This chip is 30pins long (2 x15) and 11 pins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
  H-Bridge with L298N: h-bridge
